# Fritzing sketch IIC Sketch 2 (saved by Fritzing 0.9.2b)
breadboards: 1

parts:
  Raspberry_Pi5 = Raspberry Pi 2
  Part4 = Arduino Uno (Rev3) - ICSP
  Part5 = Arduino Uno (Rev3) - ICSP

nets:
  N1: Raspberry_Pi5.GPIO2, Part4.A4/SDA, Part5.A4/SDA
  N2: Raspberry_Pi5.GPIO3, Part4.A5/SCL, Part5.A5/SCL
  GND: Raspberry_Pi5.GND, Part4.GND, Part5.GND
  5V: Raspberry_Pi5.5V, Part4.5V, Part5.5V

notes:
  GROUND
  VCC
  SLAVE 1
  SLAVE 2
  MASTER
  I2C COMMUNICATION
  SDA
  SCL
