# Fritzing sketch IOTTRAININGaNALOG (saved by Fritzing 0.9.2b)
breadboards: 1

parts:
  Raspberry_Pi3 = Raspberry Pi 2
  Part1 = Arduino Uno (Rev3) - ICSP
  R1 = TRIMPOT [package=trimpot_tc33]

nets:
  GND: Raspberry_Pi3.GND, Part1.GND, R1.CCW
  N1: Raspberry_Pi3.GPIO15, Part1.D1/TX
  N2: Raspberry_Pi3.GPIO14, Part1.D0/RX
  5V: Raspberry_Pi3.5V, Part1.5V, R1.CW
  N3: Part1.A0, R1.WIPER

notes:
  GROUND
  VCC
  POT
  Rx <- Tx
  Tx -> Rx
  UART COMMUNICATION
