# Fritzing sketch IOTtRAININGsERVO (saved by Fritzing 0.9.2b)
breadboards: 1

parts:
  Raspberry_Pi2 = Raspberry Pi 2
  J1 = Basic Servo

nets:
  GND: Raspberry_Pi2.GND, J1.gnd
  N1: Raspberry_Pi2.GPIO18, J1.pulse
  5V: Raspberry_Pi2.5V, J1.vcc

notes:
  GROUND
  VCC
  SERVO
