# Fritzing sketch SPIButton (saved by Fritzing 0.9.2b)
breadboards: 1

parts:
  Part2 = Arduino Uno (Rev3) - ICSP
  Raspberry_Pi4 = Raspberry Pi 2
  S1 = Pushbutton [package="[THT]"]
  S2 = Pushbutton [package="[THT]"]
  R1 = Resistor [tolerance=±5% resistance=220 package=THT]
  R2 = Resistor [tolerance=±5% resistance=220 package=THT]
  LED1 = LED - 5mm [color="Red (633nm)" package="5 mm [THT]"]
  LED2 = LED - 5mm [color="Red (633nm)" package="5 mm [THT]"]
  R3 = Resistor [tolerance=±5% resistance=220 package=THT]
  R4 = Resistor [tolerance=±5% resistance=220 package=THT]
  Part3 = Arduino Uno (Rev3) - ICSP
  LED3 = LED - 5mm [color="Red (633nm)" package="5 mm [THT]"]
  LED4 = LED - 5mm [color="Red (633nm)" package="5 mm [THT]"]
  R5 = Resistor [tolerance=±5% resistance=220 package=THT]
  R6 = Resistor [tolerance=±5% resistance=220 package=THT]

nets:
  N1: Part2.ICSP_MISO, Part2.D12/MISO, Raspberry_Pi4.GPIO9, Part3.D12/MISO
  N2: Part2.ICSP_SCK, Part2.D13/SCK, Raspberry_Pi4.GPIO11, Part3.D13/SCK
  N3: Part2.ICSP_MOSI, Part2.D11_PWM/MOSI, Raspberry_Pi4.GPIO10, Part3.D11_PWM/MOSI
  N4: Part2.D10_PWM/SS, Raspberry_Pi4.GPIO8
  N5: Part2.GND, R1.Pin_0, R2.Pin_0, LED1.cathode, LED2.cathode
  N6: Part2.D6_PWM, R3.Pin_0
  N7: Part2.D7, R4.Pin_0
  5V: Part2.5V, Raspberry_Pi4.5V, S1.Pin_1, S1.Pin_2, S2.Pin_1, S2.Pin_2, Part3.5V
  GND: Raspberry_Pi4.GND, Part3.GND, LED3.cathode, LED4.cathode
  N8: Raspberry_Pi4.GPIO7, Part3.D10_PWM/SS
  N9: Raspberry_Pi4.GPIO24, S1.Pin_3, S1.Pin_4, R1.Pin_1
  N10: Raspberry_Pi4.GPIO23, S2.Pin_3, S2.Pin_4, R2.Pin_1
  N11: LED1.anode, R3.Pin_1
  N12: LED2.anode, R4.Pin_1
  N13: Part3.D6_PWM, R5.Pin_0
  N14: Part3.D7, R6.Pin_0
  N15: LED3.anode, R6.Pin_1
  N16: LED4.anode, R5.Pin_1

notes:
  GROUND
  VCC
  SPI COMMUNICATION
  SLAVE 1
  SLAVE 2
  MASTER
