# Fritzing sketch TRASHCAN (saved by Fritzing 0.9.2b)
breadboards: 1

parts:
  Raspberry_Pi2 = Raspberry Pi B rev2
  J1 = screw terminal, 4 pins
  R1 = Resistor [tolerance=±5% resistance=100 package=THT]
  R2 = Resistor [tolerance=±5% resistance=220 package=THT]

nets:
  5V: Raspberry_Pi2.5V, J1.pin1
  GND: Raspberry_Pi2.GND, J1.pin4, R2.Pin_1
  N1: Raspberry_Pi2.GPIO_23, J1.pin2
  N2: J1.pin3, R1.Pin_1, R2.Pin_0

notes:
  ULTRASONIC
  SENSOR
  HC SR-04
  VOLTAGE
  DIVIDER
  VCC
  ECHO
  TRIGGER
  GND
  SMART TRASH CAN
