# Fritzing sketch iotTrainingLED (saved by Fritzing 0.9.2b)
breadboards: 1

parts:
  Raspberry_Pi1 = Raspberry Pi 2
  S1 = SWITCH-MOMENTARY-2 [package=tactile-pth-12mm]
  S2 = SWITCH-MOMENTARY-2 [package=tactile-pth-12mm]
  R1 = Resistor [tolerance=±5% resistance=10k package=THT]
  R2 = Resistor [tolerance=±5% resistance=10k package=THT]
  LED1 = LED - 5mm [color="Red (633nm)" package="5 mm [THT]"]
  LED2 = LED - 5mm [color="Red (633nm)" package="5 mm [THT]"]
  LED3 = LED - 5mm [color="Red (633nm)" package="5 mm [THT]"]
  LED4 = LED - 5mm [color="Red (633nm)" package="5 mm [THT]"]
  R3 = Resistor [tolerance=±5% resistance=220 package=THT]
  R4 = Resistor [tolerance=±5% resistance=220 package=THT]
  R5 = Resistor [tolerance=±5% resistance=220 package=THT]
  R6 = Resistor [tolerance=±5% resistance=220 package=THT]

nets:
  GND: Raspberry_Pi1.GND, R1.Pin_1, R2.Pin_1
  N1: Raspberry_Pi1.GPIO21, LED1.anode
  N2: Raspberry_Pi1.GPIO20, LED2.anode
  N3: Raspberry_Pi1.GPIO16, LED3.anode
  N4: Raspberry_Pi1.GPIO12, LED4.anode
  N5: Raspberry_Pi1.GPIO15, S2.2, R1.Pin_0
  N6: Raspberry_Pi1.GPIO14, S1.2, R2.Pin_0
  5V: Raspberry_Pi1.5V, S1.1, S2.1, R3.Pin_1, R4.Pin_1, R5.Pin_1, R6.Pin_1
  N7: LED1.cathode, R3.Pin_0
  N8: LED2.cathode, R4.Pin_0
  N9: LED3.cathode, R5.Pin_0
  N10: LED4.cathode, R6.Pin_0

notes:
  LED 1
  LED 2
  LED 3
  LED 4
  SWITCH 1
  SWITCH 2
  GROUND
  VCC
