# Fritzing sketch uartButton (saved by Fritzing 0.9.2b)
breadboards: 1

parts:
  Part2 = Arduino Uno (Rev3) - ICSP
  Raspberry_Pi4 = Raspberry Pi 2
  S1 = Pushbutton [package="[THT]"]
  S2 = Pushbutton [package="[THT]"]
  R1 = Resistor [tolerance=±5% resistance=220 package=THT]
  R2 = Resistor [tolerance=±5% resistance=220 package=THT]
  LED1 = LED - 5mm [color="Red (633nm)" package="5 mm [THT]"]
  LED2 = LED - 5mm [color="Red (633nm)" package="5 mm [THT]"]
  R3 = Resistor [tolerance=±5% resistance=220 package=THT]
  R4 = Resistor [tolerance=±5% resistance=220 package=THT]

nets:
  GND: Part2.GND, Raspberry_Pi4.GND, R1.Pin_0, R2.Pin_0, LED1.cathode, LED2.cathode
  N1: Part2.D0/RX, Raspberry_Pi4.GPIO14
  N2: Part2.D1/TX, Raspberry_Pi4.GPIO15
  N3: Part2.D6_PWM, R3.Pin_0
  N4: Part2.D7, R4.Pin_0
  N5: Part2.5V, S1.Pin_1, S1.Pin_2, S2.Pin_1
  N6: Raspberry_Pi4.GPIO7, S1.Pin_3, S1.Pin_4, R1.Pin_1
  N7: Raspberry_Pi4.GPIO8, S2.Pin_3, S2.Pin_4, R2.Pin_1
  5V: Raspberry_Pi4.5V
  N8: LED1.anode, R3.Pin_1
  N9: LED2.anode, R4.Pin_1

notes:
  Rx <- Tx
  Tx -> Rx
  GROUND
  VCC
  UART COMMUNICATION
