# Fritzing sketch yunparking (saved by Fritzing 0.9.2b)
breadboards: 1

parts:
  Part1 = Arduino Yun
  J1 = screw terminal, 4 pins
  J2 = screw terminal, 4 pins
  J3 = screw terminal, 4 pins

nets:
  N1: Part1.ICSP_MISO, Part1.D12/MISO, J1.pin2
  5V: Part1.5V, Part1.VIN, J1.pin4, J2.pin4, J3.pin4
  N2: Part1.D8, J3.pin3
  N3: Part1.D9_PWM, J3.pin2
  N4: Part1.D13/SCK, J1.pin3
  GND: Part1.GND, J1.pin1, J2.pin1, J3.pin1
  N5: Part1.D4, J2.pin3
  N6: Part1.D5_PWM, J2.pin2

notes:
  Sensor 3
  Sensor 2
  Sensor 1
  Gnd
  5V
  echo
  trigger
  ULTRASONIC
  SENSORS
  HC-SR04
  SUPPLY VOLTAGE
  GROUND
  SMART PARKING SYSTEM
